# Fritzing sketch home_monitor (saved by Fritzing 0.9.2b)

parts:
  B1 = Sparrow Nest Programming Board [part_number=SN01]
  B2 = Sparrow Wireless Sensor Node [part_number=S4]  # not connected
  PIR1 = PIR sensor
  B3 = Sparrow Nest Programming Board [part_number=SN01]  # not connected
  B4 = Sparrow Wireless Sensor Node [part_number=S4]  # not connected
  Raspberry_Pi1 = Raspberry Pi 2  # not connected

nets:
  N1: B1.D18, PIR1.SIG
  GND: B1.GND, PIR1.GND
  3V3: B1.3V3, PIR1.VDD
